# Fritzing sketch Binary Clock (saved by Fritzing 0.9.3b)
breadboards: 1

parts:
  Part1 = Arduino Leonardo (Rev3b)
  R1 = Resistor [tolerance=±5% resistance=220 package=THT]
  Minute_1 = LED - 5mm [color="Red (633nm)" package="5 mm [THT]"]
  R2 = Resistor [tolerance=±5% resistance=220 package=THT]
  Minute_2 = LED - 5mm [color="Red (633nm)" package="5 mm [THT]"]
  R3 = Resistor [tolerance=±5% resistance=220 package=THT]
  Minute_4 = LED - 5mm [color="Red (633nm)" package="5 mm [THT]"]
  R4 = Resistor [tolerance=±5% resistance=220 package=THT]
  Minute_8 = LED - 5mm [color="Red (633nm)" package="5 mm [THT]"]
  R5 = Resistor [tolerance=±5% resistance=220 package=THT]
  Minute_16 = LED - 5mm [color="Red (633nm)" package="5 mm [THT]"]
  R6 = Resistor [tolerance=±5% resistance=220 package=THT]
  Minute_32 = LED - 5mm [color="Red (633nm)" package="5 mm [THT]"]
  R7 = Resistor [tolerance=±5% resistance=220 package=THT]
  Hour_1 = LED - 5mm [color="Blue (470nm)" package="5 mm [THT]"]
  R8 = Resistor [tolerance=±5% resistance=220 package=THT]
  Hour_2 = LED - 5mm [color="Blue (470nm)" package="5 mm [THT]"]
  R9 = Resistor [tolerance=±5% resistance=220 package=THT]
  Hour_4 = LED - 5mm [color="Blue (470nm)" package="5 mm [THT]"]
  R10 = Resistor [tolerance=±5% resistance=220 package=THT]
  Hour_8 = LED - 5mm [color="Blue (470nm)" package="5 mm [THT]"]
  R11 = Resistor [tolerance=±5% resistance=220 package=THT]
  Hour_16 = LED - 5mm [color="Blue (470nm)" package="5 mm [THT]"]
  RTC1 = Generic male header - 6 pins [form="♂ (male)" package=THT]

nets:
  N1: Part1.D1/TX, Minute_1.cathode
  N2: Part1.D4/A6, Minute_2.cathode
  N3: Part1.D5_PWM, Minute_4.cathode
  N4: Part1.D6_PWM/A7, Minute_8.cathode
  N5: Part1.D7, Minute_16.cathode
  N6: Part1.5V, RTC1.pin5
  N7: Part1.GND, R1.Pin_1, R2.Pin_1, R3.Pin_1, R4.Pin_1, R5.Pin_1, R6.Pin_1, R7.Pin_1, R8.Pin_1, R9.Pin_1, R10.Pin_1, R11.Pin_1, RTC1.pin6
  N8: Part1.D8/A8, Minute_32.cathode
  N9: Part1.D9_PWM/A9, Hour_1.cathode
  N10: Part1.D10_PWM/A10, Hour_2.cathode
  N11: Part1.D11_PWM, Hour_4.cathode
  N12: Part1.D12/A11, Hour_8.cathode
  N13: Part1.D13_PWM, Hour_16.cathode
  N14: Part1.SDA, RTC1.pin4
  N15: Part1.SCL, RTC1.pin3
  N16: R1.Pin_0, Minute_1.anode
  N17: R2.Pin_0, Minute_2.anode
  N18: R3.Pin_0, Minute_4.anode
  N19: R4.Pin_0, Minute_8.anode
  N20: R5.Pin_0, Minute_16.anode
  N21: R6.Pin_0, Minute_32.anode
  N22: R7.Pin_0, Hour_1.anode
  N23: R8.Pin_0, Hour_2.anode
  N24: R9.Pin_0, Hour_4.anode
  N25: R10.Pin_0, Hour_8.anode
  N26: R11.Pin_0, Hour_16.anode

custom parts:
  Generic male header - 6 pins: Generic male header
